# Fritzing sketch webserver_Waterlvl_Schema (saved by Fritzing 0.9.3b)
breadboards: 1

parts:
  Water_Level_Sensor = Water Level Sensor
  U1 = NodeMCU V3.0
  Q1 = Basic FET P-Channel [package="D2Pak [SMD]"]
  R2 = Resistor [tolerance=±5% resistance=10k package="0805 [SMD]"]
  R3 = Resistor [tolerance=±5% resistance=10k package="0805 [SMD]"]
  R1 = Resistor [tolerance=±5% resistance=10k package="0805 [SMD]"]

nets:
  N1: Water_Level_Sensor.SIG, R2.Pin_1
  GND: Water_Level_Sensor.GND, U1.GND, R3.Pin_0, R1.Pin_0
  N2: U1.D5, Q1.Gate, R1.Pin_1
  N3: U1.A0, R2.Pin_0, R3.Pin_1

notes:
  Alimentation externe
  Alimentation pompe

custom parts:
  Water Level Sensor: A water level sensor. This sensor operates at 3V to 5V. The Sig (signal) pin outputs an analogue signal that is in proportion to the amount of water in contact with the sensor.
  NodeMCU V3.0: ESP8266 based NodeMCU
